# Fritzing sketch Schematic Diagram (saved by Fritzing 0.9.2b)
breadboards: 1

parts:
  Part1 = Arduino Uno (Rev3) - ICSP
  LED1 = LEDs [package=led10mm]
  OLED_I2C1 = OLED 128x64 I2C Monochrome Display
  Mod1 = gy-906
  M1 = fc-51 [package=THT]
  LED2 = smd LED [color="Red (633nm)" package="1206 [SMD]"]

nets:
  N1: Part1.A4/SDA, OLED_I2C1.SDA, Mod1.SDA
  N2: Part1.A5/SCL, OLED_I2C1.SCK, Mod1.SCL
  N3: Part1.ICSP_MISO, Part1.D12/MISO, LED1.A
  N4: Part1.ICSP_MOSI, Part1.D11_PWM/MOSI, LED2.anode
  N5: Part1.D8, M1.pin1
  3V3: Part1.3V3, Mod1.VIN
  5V: Part1.5V, OLED_I2C1.VDD, M1.pin3
  GND: Part1.GND, LED1.C, OLED_I2C1.GND, Mod1.GND, M1.pin2, LED2.cathode

custom parts:
  gy-906: gy-906 Non-contact PIR I2C interface temperature sensor breakout board.

// code stored in the sketch: SKetch.ino
#include <SPI.h>
#include <Wire.h>
#include <Adafruit_GFX.h>
#include <Adafruit_SSD1306.h>
#include <Adafruit_MLX90614.h>
#include <Fonts/FreeMonoBold12pt7b.h>
#include <Fonts/FreeSans9pt7b.h>

#define SCREEN_WIDTH 128 
#define SCREEN_HEIGHT 64 
#define OLED_RESET     4 // Reset pin # (or -1 if sharing Arduino reset pin)
#define SCREEN_ADDRESS 0x3C 
Adafruit_SSD1306 display(SCREEN_WIDTH, SCREEN_HEIGHT, &Wire, OLED_RESET);
Adafruit_MLX90614 mlx = Adafruit_MLX90614();

int stat;
int irsensor = 8;
int red = 11;
int green = 12;

void setup() {
  Serial.begin(9600);
  Serial.println("Serial Initialized");
  mlx.begin();
    // SSD1306_SWITCHCAPVCC = generate display voltage from 3.3V internally
  if(!display.begin(SSD1306_SWITCHCAPVCC, SCREEN_ADDRESS)) {
    Serial.println(F("SSD1306 allocation failed"));
    for(;;); // Don't proceed, loop forever
  }
  delay(2000); // Pause for 2 seconds
  display.display();
  // Clear the buffer
  display.clearDisplay();
  
  pinMode(red, OUTPUT);
  pinMode(green, OUTPUT);
  pinMode(irsensor, INPUT);
}

void loop() {
  
  stat = digitalRead(irsensor);
  switch (stat){
    case HIGH :
    display.clearDisplay();
    digitalWrite(green, 0);
    digitalWrite(red, 1);
    printKosong();
    display.clearDisplay();
    break;
    
    case LOW :
    display.clearDisplay();
    digitalWrite(green, 1);
    digitalWrite(red, 0);
    printSuhu();
    display.clearDisplay();
    break;
    
    default :
    display.clearDisplay();
    printKosong();
    digitalWrite(red, 1); 
    break;
  }
  
}

void printKosong(){

  display.setFont(&FreeSans9pt7b);
  display.setTextColor(WHITE);        // Draw white text
  display.setCursor(0,30);
  display.print("Objek Tidak");
  
  display.setTextColor(WHITE);        // Draw white text
  display.setCursor(0, 50);
  display.print("Terdeteksi");
  Serial.println("Tidak ada objek");
  delay(1000);
  display.display();
}

void printSuhu() {
  display.setFont(&FreeSans9pt7b);
  display.setTextColor(WHITE);        // Draw white text
  display.setCursor(0,30);
  display.print("Suhu :");
  
  display.setFont(&FreeMonoBold12pt7b);
  display.setTextColor(WHITE);        // Draw white text
  display.setCursor(0, 50);
  display.print(mlx.readObjectTempC(),1);
  display.drawCircle(92, 35, 3, WHITE);
  display.setCursor(100, 50);
  display.print("C");
  Serial.println(mlx.readObjectTempC());
  delay(1000);
  display.display();
}
